# Fritzing sketch TMP36_MCP3008_Breadboard (saved by Fritzing 0.9.4)
breadboards: 1

parts:
  U1 = TMP36 [package=to-92-kit]
  ADC1 = MCP3008 [package=dil16]
  Raspberry_Pi_1 = Raspberry Pi 3 [part_number=RPI-3-V1.2]

nets:
  VCC: U1.VCC, ADC1.VREF, ADC1.VDD, Raspberry_Pi_1.3v3
  N1: U1.VOUT, ADC1.CH0
  GND: U1.GND, ADC1.DGND, ADC1.AGND, Raspberry_Pi_1.GND
  N2: ADC1.CS/SHDN, Raspberry_Pi_1.GIPO22
  N3: ADC1.Din, Raspberry_Pi_1.GIPO10
  N4: ADC1.Dout, Raspberry_Pi_1.GIPO9
  N5: ADC1.CLK, Raspberry_Pi_1.GIPO11
